# Fritzing sketch circuit (saved by Fritzing 0.9.2b)
breadboards: 1

parts:
  Part1 = Arduino Uno (Rev3)
  J1 = Piezo Speaker
  R1 = Resistor [tolerance=±5% resistance=220 package=THT]
  R2 = Resistor [tolerance=±5% resistance=220 package="2512 [SMD]"]
  R3 = Resistor [tolerance=±5% resistance=220 package="2512 [SMD]"]
  R4 = Resistor [tolerance=±5% resistance=220 package="2512 [SMD]"]
  LED1 = RGB LED (com. anode, rbg) [package="5 mm [THT]"]

nets:
  N1: Part1.D10_PWM/SS, J1.pin2
  N2: Part1.D11_PWM/MOSI, R4.Pin_1
  N3: Part1.D12/MISO, R3.Pin_1
  N4: Part1.D13/SCK, R2.Pin_1
  N5: Part1.GND, R1.Pin_1, LED1.common_anode
  N6: J1.pin1, R1.Pin_0
  N7: R2.Pin_0, LED1.red_cathode
  N8: R3.Pin_0, LED1.green_cathode
  N9: R4.Pin_0, LED1.blue_cathode
